// Logisim project BCD_7Seg_Decoder.circ as structural Verilog: 1 circuit, main circuit main
module main (
  input  l,
  input  m,
  input  n,
  input  o
);

  wire a_out, and_1_out, and_2_out, and_3_out, and_4_out, and_5_out, and_6_out, and_7_out, and_8_out,
       and_9_out, and_10_out, and_11_out, and_12_out, b_out, c_out, d_out, e_out, f_out, g_out, not_1_out,
       not_2_out, not_3_out, not_4_out, not_5_out, not_6_out, not_7_out, not_8_out, not_9_out, not_10_out,
       not_11_out, not_12_out, not_13_out, not_14_out, not_15_out, not_16_out, not_17_out, not_18_out,
       not_19_out, or_1_out, or_2_out, or_3_out, or_4_out, or_5_out, or_6_out, or_7_out, or_8_out, or_9_out,
       or_10_out, or_11_out, xor_1_out, xor_2_out;

  not not_1 (not_1_out, n);
  not not_2 (not_2_out, m);
  not not_3 (not_3_out, n);
  not not_4 (not_4_out, o);
  not not_5 (not_5_out, o);
  not not_6 (not_6_out, m);
  not not_7 (not_7_out, n);
  not not_8 (not_8_out, o);
  not not_9 (not_9_out, n);
  not not_10 (not_10_out, l);
  not not_11 (not_11_out, m);
  xor xor_1 (xor_1_out, m, o);
  not not_12 (not_12_out, xor_1_out);
  or or_1 (or_1_out, l, n);
  xor xor_2 (xor_2_out, n, o);
  not not_13 (not_13_out, xor_2_out);
  not not_14 (not_14_out, m);
  or or_2 (or_2_out, l, m);
  or or_3 (or_3_out, not_1_out, o);
  not not_15 (not_15_out, o);
  not not_16 (not_16_out, m);
  not not_17 (not_17_out, o);
  not not_18 (not_18_out, o);
  and and_1 (and_1_out, n, not_8_out);
  and and_2 (and_2_out, m, not_9_out);
  and and_3 (and_3_out, not_10_out, not_11_out);
  or a (a_out, not_12_out, or_1_out);
  or or_4 (or_4_out, not_14_out, l);
  or c (c_out, or_2_out, or_3_out);
  and and_4 (and_4_out, not_15_out, not_2_out);
  and and_5 (and_5_out, not_3_out, o);
  and and_6 (and_6_out, not_4_out, n);
  or or_5 (or_5_out, not_6_out, n);
  or or_6 (or_6_out, l, and_7_out);
  and and_7 (and_7_out, not_17_out, not_7_out);
  not not_19 (not_19_out, n);
  and and_8 (and_8_out, and_3_out, n);
  or b (b_out, not_13_out, or_4_out);
  or or_7 (or_7_out, and_4_out, and_9_out);
  and and_9 (and_9_out, n, not_16_out);
  and and_10 (and_10_out, and_5_out, m);
  and e (e_out, not_5_out, or_5_out);
  and and_11 (and_11_out, m, not_18_out);
  or or_8 (or_8_out, and_1_out, and_2_out);
  or or_9 (or_9_out, and_8_out, l);
  or d (d_out, or_7_out, or_10_out);
  or or_10 (or_10_out, and_10_out, and_6_out);
  or or_11 (or_11_out, not_19_out, and_11_out);
  or g (g_out, or_8_out, or_9_out);
  and and_12 (and_12_out, m, or_11_out);
  _7_Segment_Display disp (.g(g_out), .f(f_out), .a(a_out), .b(b_out), .e(e_out), .d(d_out), .c(c_out));  // open: dp
  or f (f_out, or_6_out, and_12_out);
endmodule
